// Logisim project cpu.circ as structural Verilog: 1 circuit, main circuit cpu
module cpu (
  input  clk,
  input  [31:0] INSTRUCTION,
  input  [31:0] READ_DATA,
  output [31:0] WRITE_ADDRESS,
  output [31:0] PROGRAM_COUNTER,
  output [31:0] ra,
  output [31:0] sp,
  output [31:0] t0,
  output [31:0] t1,
  output [31:0] t2,
  output [31:0] s0,
  output [31:0] s1,
  output [31:0] a0,
  output [31:0] tohost,
  output [3:0] WRITE_ENABLE,
  output [31:0] WRITE_DATA
);

  wire ASel, BrEq, BrLt, BrUn, BSel, CSRSel, CSRWen, IF_ID_PCSel, MemRW, PCSel, RegWEn;
  wire [1:0] WBSel;
  wire [2:0] ImmSel;
  wire [3:0] ALUSel;
  wire [31:0] adder_1_out, bit_extender_1_out, CSR_din, FINAL_INSTRUCTION, IF_ID_INSTRUCTION, IF_ID_PC,
       IF_ID_PC_Plus_4, imm, multiplexer_1_out, multiplexer_4_out, multiplexer_5_out, Read_Data_1,
       Write_Data_Reg;

  Adder #(.width(32)) adder_1 (.a(PROGRAM_COUNTER), .b(32'h4), .out(adder_1_out));  // open: cin, cout
  Multiplexer #(.enable("false"), .width(32)) multiplexer_1 (
    .in0(adder_1_out), .in1(WRITE_ADDRESS), .out(multiplexer_1_out), .sel(PCSel));
  Register #(.width(32)) PC (.D(multiplexer_1_out), .clk(clk), .Q(PROGRAM_COUNTER));  // open: en, clr
  Register #(.width(32)) register_1 (.D(PROGRAM_COUNTER), .clk(clk), .Q(IF_ID_PC));  // open: en, clr
  Register #(.width(32)) register_2 (.D(INSTRUCTION), .clk(clk), .Q(IF_ID_INSTRUCTION));  // open: en, clr
  Register #(.width(1)) register_3 (.D(PCSel), .clk(clk), .Q(IF_ID_PCSel));  // open: en, clr
  control_logic control_logic_1 (
    .CSRWen(CSRWen), .PCSel(PCSel), .RegWEn(RegWEn), .ImmSel(ImmSel), .BrUn(BrUn), .ASel(ASel), .BSel(BSel),
    .ALUSel(ALUSel), .MemRW(MemRW), .WBSel(WBSel), .CSRSel(CSRSel), .inst(FINAL_INSTRUCTION), .BrEq(BrEq),
    .BrLt(BrLt));
  Multiplexer #(.enable("false"), .width(32)) multiplexer_2 (
    .in0(IF_ID_INSTRUCTION), .in1(32'h13), .out(FINAL_INSTRUCTION), .sel(IF_ID_PCSel));
  imm_gen imm_gen_1 (.inst(FINAL_INSTRUCTION), .ImmSel(ImmSel), .imm(imm));
  regfile regfile_1 (
    .rs1(FINAL_INSTRUCTION[19:15]), .rs2(FINAL_INSTRUCTION[24:20]), .rd(FINAL_INSTRUCTION[11:7]),
    .Write_Data(Write_Data_Reg), .RegWEn(RegWEn), .clk(clk), .ra(ra), .sp(sp), .t0(t0), .t1(t1), .t2(t2),
    .s0(s0), .s1(s1), .a0(a0), .Read_Data_1(Read_Data_1), .Read_Data_2(WRITE_DATA));
  assign bit_extender_1_out = {{27{1'b0}}, FINAL_INSTRUCTION[19:15]};  // Bit_Extender bit_extender_1
  Multiplexer #(.enable("false"), .width(32)) multiplexer_3 (
    .in0(Read_Data_1), .in1(bit_extender_1_out), .out(CSR_din), .sel(CSRSel));
  branch_comp branch_comp_1 (.rs1(Read_Data_1), .rs2(WRITE_DATA), .BrUn(BrUn), .BrEq(BrEq), .BrLt(BrLt));
  csr csr_1 (.CSR_din(CSR_din), .CSR_WE(CSRWen), .clk(clk), .tohost(tohost));  // open: CSR_address
  Multiplexer #(.enable("false"), .width(32)) multiplexer_4 (
    .in0(Read_Data_1), .in1(IF_ID_PC), .out(multiplexer_4_out), .sel(ASel));
  Multiplexer #(.enable("false"), .width(32)) multiplexer_5 (
    .in0(WRITE_DATA), .in1(imm), .out(multiplexer_5_out), .sel(BSel));
  alu alu_1 (.Result(WRITE_ADDRESS), .A(multiplexer_4_out), .B(multiplexer_5_out), .ALUSel(ALUSel));
  assign WRITE_ENABLE = {{3{MemRW}}, MemRW};  // Bit_Extender bit_extender_2
  Adder #(.width(32)) adder_2 (.a(IF_ID_PC), .b(32'h4), .out(IF_ID_PC_Plus_4));  // open: cin, cout
  Multiplexer #(.enable("false"), .select(2), .width(32)) multiplexer_6 (
    .in0(WRITE_ADDRESS), .in1(READ_DATA), .in2(IF_ID_PC_Plus_4), .out(Write_Data_Reg), .sel(WBSel));  // open: in3

  // Other names for the same wires on the sheet: ALUOut[31:0] = WRITE_ADDRESS; opt_code[6:0] = FINAL_INSTRUCTION[6:0];
  //   rd[4:0] = FINAL_INSTRUCTION[11:7]; rs1[4:0] = FINAL_INSTRUCTION[19:15]; rs2[4:0] = FINAL_INSTRUCTION[24:20];
  //   Read_Data_2[31:0] = WRITE_DATA

  // Notes on the sheet:
  //   Output to IMEM
  //   IMEM (do **NOT** move this)
  //   Inputs from IMEM
  //   It is OK to move the PC, RegFile, ALU, MEM, Branch Comp, Imm Gen, and Control Logic to wherever is most convenient for you when constructing your CPU, and to delete this text
  //   Inputs/Outputs for testing. Do **NOT** move these.
  //   Outputs To DMEM
  //   DMEM (do **NOT** move this)
  //   Inputs From DMEM
endmodule
